# Fritzing sketch Botão - PULL_UP (saved by Fritzing 0.9.3b)
breadboards: 1

parts:
  R1 = Resistor [tolerance=±5% resistance=220 package=THT]
  Componente1 = Arduino Uno (Rev3) - ICSP
  LED1 = smd LED [color="Red (633nm)" package="0603 [SMD]"]
  S1 = Pushbutton [package="[SMD]"]
  LED2 = smd LED [color="Red (633nm)" package="0603 [SMD]"]
  S2 = Pushbutton [package="[SMD]"]
  R2 = Resistor [tolerance=±5% resistance=220 package=THT]
  LED3 = smd LED [color="Red (633nm)" package="0603 [SMD]"]
  S3 = Pushbutton [package="[SMD]"]
  R3 = Resistor [tolerance=±5% resistance=220 package=THT]
  S4 = Pushbutton [package="[SMD]"]
  LED4 = smd LED [color="Red (633nm)" package="0603 [SMD]"]
  R4 = Resistor [tolerance=±5% resistance=220 package=THT]

nets:
  N1: R1.Pin_0, LED1.cathode
  N2: R1.Pin_1, Componente1.GND, S1.Pin_1, S1.Pin_2, S2.Pin_1, S2.Pin_2, R2.Pin_1, S3.Pin_1, S3.Pin_2, R3.Pin_1, S4.Pin_1, S4.Pin_2, R4.Pin_1
  N3: Componente1.D8, S1.Pin_3, S1.Pin_4
  N4: Componente1.D9_PWM, S2.Pin_3, S2.Pin_4
  N5: Componente1.D10_PWM/SS, S3.Pin_3, S3.Pin_4
  N6: Componente1.D11_PWM/MOSI, S4.Pin_3, S4.Pin_4
  N7: Componente1.D1/TX, LED1.anode
  N8: Componente1.D2, LED2.anode
  N9: Componente1.D3_PWM, LED3.anode
  N10: Componente1.D4, LED4.anode
  N11: LED2.cathode, R2.Pin_0
  N12: LED3.cathode, R3.Pin_0
  N13: LED4.cathode, R4.Pin_0
