# Fritzing sketch LED - Circuit (saved by Fritzing 0.9.3b)
breadboards: 1

parts:
  LED1 = smd LED [color="Red (633nm)" package="1206 [SMD]"]
  R1 = Resistor [tolerance=±5% resistance=220 package=THT]
  Componente1 = Arduino Uno (Rev3) - ICSP
  Componente1_2 = Arduino Uno (Rev3) - ICSP
  S1 = Pushbutton [package="[THT]"]  # not connected

nets:
  N1: LED1.cathode, R1.Pin_1
  N2: LED1.anode, Componente1_2.D2
  GND: R1.Pin_0, Componente1.GND, Componente1_2.GND
